# Fritzing sketch dogscale strip board (saved by Fritzing 1.0.1rc)
stripboards: 2

parts:
  S1 = Load Sensor - 50kg [part_number=SEN-10245]
  S2 = Load Sensor - 50kg [part_number=SEN-10245]
  S3 = Load Sensor - 50kg [part_number=SEN-10245]
  S4 = Load Sensor - 50kg [part_number=SEN-10245]
  Bauteil2 = HX711 Weighing Sensor Module MR
  A1 = SparkFun RJ45 Breakout v11  # not connected
  LCD2 = 2.8" SPI TFT Module [part_number=MSP2807]
  Mod3 = Amica NodeMCU DEVKIT 1.0
  A3 = SparkFun RJ45 Breakout v11
  J1 = female pin header, 4 pins [form="♀ (female)"]
  J2 = female pin header, 6 pins [form="♀ (female)"]
  J3 = female pin header, 15 pins [form="♀ (female)"]
  J4 = female pin header, 15 pins [form="♀ (female)"]
  J5 = female pin header, 14 pins [form="♀ (female)"]

nets:
  N1: S1.B, S2.B
  N2: S1.W, S4.W
  N3: S2.W, S3.W
  N4: S3.B, S4.B
  N5: Bauteil2.VCC, J1.pin1
  N6: Bauteil2.GND, J1.pin4
  N7: Bauteil2.DT, J1.pin3
  N8: Bauteil2.SCK, J1.pin2
  N9: Bauteil2.E+, J2.pin6
  N10: Bauteil2.E-, J2.pin5
  N11: Bauteil2.A-, J2.pin4
  N12: Bauteil2.A+, J2.pin3
  N13: Bauteil2.B-, J2.pin2
  N14: Bauteil2.B+, J2.pin1
  N15: LCD2.pin1, LCD2.pin8, Mod3.pin1, Mod3.pin_10, Mod3.pin_26, A3.Pin_3, J3.pin1, J3.pin10, J4.pin5, J5.pin1, J5.pin8
  N16: LCD2.pin2, Mod3.pin2, Mod3.pin_9, Mod3.pin_25, Mod3.pin_29, A3.Pin_6, J3.pin2, J3.pin9, J4.pin2, J4.pin6, J5.pin2
  N17: LCD2.pin3, Mod3.pin5, J3.pin5, J5.pin3
  N18: LCD2.pin4, Mod3.pin_11, J3.pin11, J5.pin4
  N19: LCD2.pin5, Mod3.pin_12, J3.pin12, J5.pin5
  N20: LCD2.pin6, LCD2.pin12, Mod3.pin6, J3.pin6, J5.pin6, J5.pin12
  N21: LCD2.pin7, LCD2.pin10, Mod3.pin8, J3.pin8, J5.pin7, J5.pin10
  N22: LCD2.pin9, LCD2.pin13, Mod3.pin7, J3.pin7, J5.pin9, J5.pin13
  N23: LCD2.pin11, Mod3.pin_15, J3.pin15, J5.pin11
  N24: LCD2.pin14, J5.pin14
  N25: Mod3.pin3, J3.pin3
  N26: Mod3.pin4, J3.pin4
  N27: Mod3.pin_13, A3.Pin_5, J3.pin13
  N28: Mod3.pin_14, A3.Pin_4, J3.pin14
  N29: Mod3.pin_16, J4.pin15
  N30: Mod3.pin_17, J4.pin14
  N31: Mod3.pin_18, J4.pin13
  N32: Mod3.pin_19, J4.pin12
  N33: Mod3.pin_20, J4.pin11
  N34: Mod3.pin_21, J4.pin10
  N35: Mod3.pin_22, J4.pin9
  N36: Mod3.pin_23, J4.pin8
  N37: Mod3.pin_24, J4.pin7
  N38: Mod3.pin_27, J4.pin4
  N39: Mod3.pin_28, J4.pin3
  N40: Mod3.pin_30, J4.pin1

notes:
  1
  2
  3
  4

custom parts:
  Load Sensor - 50kg: Half-wheatstone bridge Load Cell modified from the Fritzing Repo This load sensor, sometimes called a strain gauge, is the same one found in digital bathroom scales (you know, the ones you use in January for your New Year's resolutions, and then forget about a month later). This sensor can measure up to about 110 pounds.
  HX711 Weighing Sensor Module MR: HX711 is a precision 24-bit analog-to-digital converter (ADC) designed for weigh scales and industrial control applications to interface directly with a bridge sensor.
  SparkFun RJ45 Breakout v11: SparkFun RJ45 Breakout v11 breakout board.
  2.8" SPI TFT Module: A generic 2.8 inch LCD TFT 320x240 display with touchscreen and SD card slot. Uses the ILI9341 controller, like the Adafruit displays of this size uses.
