# Fritzing sketch dogscale (saved by Fritzing 1.0.1rc)
breadboards: 1

parts:
  Mod1 = Amica NodeMCU DEVKIT 1.0
  TFT1 = 1.44" SPI TFT Graphics Display 128x128 - MR 8pin [package=THT]
  S1 = Load Sensor - 50kg [part_number=SEN-10245]
  S2 = Load Sensor - 50kg [part_number=SEN-10245]
  S3 = Load Sensor - 50kg [part_number=SEN-10245]
  S4 = Load Sensor - 50kg [part_number=SEN-10245]
  Bauteil2 = HX711 Weighing Sensor Module MR
  Sensor1 = TTP223B Capacitive Touch Sensor Module
  A1 = SparkFun RJ45 Breakout v11
  A2 = SparkFun RJ45 Breakout v11

nets:
  N1: Mod1.pin1, Mod1.pin_10, Mod1.pin_26
  N2: Mod1.pin2, Mod1.pin_9, Mod1.pin_25, Mod1.pin_29, TFT1.pin2, Sensor1.GND, A2.Pin_4
  N3: Mod1.pin5, TFT1.pin3
  N4: Mod1.pin6, TFT1.pin6
  N5: Mod1.pin7, TFT1.pin5
  N6: Mod1.pin8, TFT1.pin7
  N7: Mod1.pin_13, A2.Pin_3
  N8: Mod1.pin_14, A2.Pin_2
  N9: Mod1.pin_15, Sensor1.SIG
  N10: Mod1.pin_28, TFT1.pin4
  N11: TFT1.pin1, TFT1.pin8, Sensor1.VCC, A2.Pin_1
  N12: S1.B, S2.B
  N13: S1.W, S4.W
  N14: S1.R, Bauteil2.A-
  N15: S2.W, S3.W
  N16: S2.R, Bauteil2.E+
  N17: S3.B, S4.B
  N18: S3.R, Bauteil2.A+
  N19: S4.R, Bauteil2.E-
  N20: Bauteil2.VCC, A1.Pin_1
  N21: Bauteil2.GND, A1.Pin_4
  N22: Bauteil2.DT, A1.Pin_3
  N23: Bauteil2.SCK, A1.Pin_2

custom parts:
  Load Sensor - 50kg: Half-wheatstone bridge Load Cell modified from the Fritzing Repo This load sensor, sometimes called a strain gauge, is the same one found in digital bathroom scales (you know, the ones you use in January for your New Year's resolutions, and then forget about a month later). This sensor can measure up to about 110 pounds.
  HX711 Weighing Sensor Module MR: HX711 is a precision 24-bit analog-to-digital converter (ADC) designed for weigh scales and industrial control applications to interface directly with a bridge sensor.
  TTP223B Capacitive Touch Sensor Module: The TTP223B capacitive touch sensor module uses the TTP223B IC. The appropriate voltage is approximately 2 to 5.5 volts.
  SparkFun RJ45 Breakout v11: SparkFun RJ45 Breakout v11 breakout board.
